# Fritzing sketch temp2iot (saved by Fritzing 0.9.5d)

parts:
  WeMos_D1_Mini1 = WeMos D1 Mini
  R1 = Resistor [tolerance=±5% resistance=220 package=THT]
  DS1 = DS18B20 1-Wire Temperature Sensor [part_number=DS18B20]

nets:
  5V: WeMos_D1_Mini1.5V, R1.Pin_1, DS1.VDD
  N1: WeMos_D1_Mini1.D3, R1.Pin_0, DS1.DQ
  N2: WeMos_D1_Mini1.G, DS1.GND
